# Fritzing sketch potentiometer (saved by Fritzing 1.0.1rc)
breadboards: 1

parts:
  Bela1 = Bela
  U2 = POT [knob_status=50% power=0.5W package=pot_alpha_rv16af-20]

nets:
  N1: Bela1.P9_01_GND, U2.A
  N2: Bela1.P9_03_3.3V, U2.E
  N3: Bela1.AIN_0, U2.S

custom parts:
  Bela: A Fritzing part for Bela
